// Logisim project COE301Project-VF.circ as structural Verilog: 5 circuits, main circuit register_file
module register_file (
  input  [2:0] rs1,
  input  [2:0] rw,
  input  [2:0] rs2,
  input  Regwrite,
  input  [15:0] BusW,
  output [15:0] BusA,
  output [15:0] BusB
);

  wire and_1_out, and_2_out, and_3_out, and_4_out, and_5_out, and_6_out, and_7_out, clock_1_out,
       decoder_1_out0, decoder_1_out1, decoder_1_out2, decoder_1_out3, decoder_1_out4, decoder_1_out5,
       decoder_1_out6, decoder_1_out7;
  wire [15:0] R1_q, R2_q, R3_q, R4_q, R5_q, R6_q, R7_q;

  Decoder #(.select(3), .enable("false")) decoder_1 (
    .out0(decoder_1_out0), .out1(decoder_1_out1), .out2(decoder_1_out2), .out3(decoder_1_out3),
    .out4(decoder_1_out4), .out5(decoder_1_out5), .out6(decoder_1_out6), .out7(decoder_1_out7), .sel(rw));
  and and_1 (and_1_out, decoder_1_out1, Regwrite);
  and and_2 (and_2_out, decoder_1_out2, Regwrite);
  and and_3 (and_3_out, decoder_1_out3, Regwrite);
  and and_4 (and_4_out, decoder_1_out4, Regwrite);
  and and_5 (and_5_out, decoder_1_out5, Regwrite);
  and and_6 (and_6_out, decoder_1_out6, Regwrite);
  and and_7 (and_7_out, decoder_1_out7, Regwrite);
  Clock clock_1 (.out(clock_1_out));
  Register #(.width(16)) R1 (.D(BusW), .en(and_1_out), .Q(R1_q), .clk(clock_1_out));  // open: clr
  Register #(.width(16)) R2 (.D(BusW), .en(and_2_out), .Q(R2_q), .clk(clock_1_out));  // open: clr
  Register #(.width(16)) R3 (.D(BusW), .en(and_3_out), .Q(R3_q), .clk(clock_1_out));  // open: clr
  Register #(.width(16)) R4 (.D(BusW), .en(and_4_out), .Q(R4_q), .clk(clock_1_out));  // open: clr
  Register #(.width(16)) R5 (.D(BusW), .en(and_5_out), .Q(R5_q), .clk(clock_1_out));  // open: clr
  Register #(.width(16)) R6 (.D(BusW), .en(and_6_out), .Q(R6_q), .clk(clock_1_out));  // open: clr
  Register #(.width(16)) R7 (.D(BusW), .en(and_7_out), .Q(R7_q), .clk(clock_1_out));  // open: clr
  Multiplexer #(.select(3), .width(16), .enable("false")) multiplexer_1 (
    .in0({16{1'b0}}), .in1(R1_q), .in2(R2_q), .in3(R3_q), .in4(R4_q), .in5(R5_q), .in6(R6_q), .in7(R7_q),
    .out(BusA), .sel(rs1));
  Multiplexer #(.select(3), .width(16), .enable("false")) multiplexer_2 (
    .in0({16{1'b0}}), .in1(R1_q), .in2(R2_q), .in3(R3_q), .in4(R4_q), .in5(R5_q), .in6(R6_q), .in7(R7_q),
    .out(BusB), .sel(rs2));
endmodule

module ALU (
  input  [15:0] BusA,
  input  [15:0] BusB,
  input  [3:0] rd,
  output [15:0] out
);

  wire comparator_1_lt, comparator_2_lt;
  wire [15:0] adder_1_out, and_1_out, bit_extender_1_out, bit_extender_2_out, nor_1_out, or_1_out,
       shifter_1_out, shifter_2_out, shifter_3_out, shifter_4_out, subtractor_1_out, xor_1_out;

  assign nor_1_out = ~(BusA | BusB);  // NOR_Gate nor_1, 16 bits wide
  assign or_1_out = BusA | BusB;  // OR_Gate or_1, 16 bits wide
  assign and_1_out = BusA & BusB;  // AND_Gate and_1, 16 bits wide
  Shifter #(.width(16)) shifter_1 (.in(BusA), .\dist (BusB[3:0]), .out(shifter_1_out));
  assign xor_1_out = BusA ^ BusB;  // XOR_Gate xor_1, 16 bits wide
  Shifter #(.width(16), .shift("lr")) shifter_2 (.in(BusA), .\dist (BusB[3:0]), .out(shifter_2_out));
  Shifter #(.width(16), .shift("ar")) shifter_3 (.in(BusA), .\dist (BusB[3:0]), .out(shifter_3_out));
  Comparator #(.width(16), .mode("unsigned")) comparator_1 (.a(BusA), .b(BusB), .lt(comparator_1_lt));  // open: gt, eq
  assign bit_extender_1_out = {{15{1'b0}}, comparator_1_lt};  // Bit_Extender bit_extender_1
  Shifter #(.width(16), .shift("rr")) shifter_4 (.in(BusA), .\dist (BusB[3:0]), .out(shifter_4_out));
  Comparator #(.width(16)) comparator_2 (.a(BusA), .b(BusB), .lt(comparator_2_lt));  // open: gt, eq
  assign bit_extender_2_out = {{15{1'b0}}, comparator_2_lt};  // Bit_Extender bit_extender_2
  Adder #(.width(16)) adder_1 (.a(BusA), .b(BusB), .out(adder_1_out));  // open: cin, cout
  Subtractor #(.width(16)) subtractor_1 (.a(BusA), .b(BusB), .out(subtractor_1_out));  // open: bin, bout
  Multiplexer #(.select(4), .width(16), .enable("false")) multiplexer_1 (
    .in0(adder_1_out), .in1(subtractor_1_out), .in2(bit_extender_2_out), .in3(bit_extender_1_out),
    .in4(xor_1_out), .in5(or_1_out), .in6(and_1_out), .in7(nor_1_out), .in8(shifter_1_out),
    .in9(shifter_2_out), .in10(shifter_3_out), .in11(shifter_4_out), .in12({BusB[10:0], {5{1'b0}}}),
    .out(out), .sel(rd));  // open: in13, in14, in15
endmodule

module ControlUnit (
  input  [4:0] op,
  input  [1:0] f,
  output [1:0] busW,
  output MemRead,
  output MemWrite,
  output [1:0] aluB,
  output RegWrite,
  output [1:0] RegDist,
  output [3:0] aluop
);

  wire comparator_1_gt;
  wire [3:0] rom_2_data;

  Comparator #(.width(5)) comparator_1 (.a(op), .b(5'b00010), .gt(comparator_1_gt));  // open: eq, lt
  ROM #(.addrWidth(5), .dataWidth(9)) rom_1 (
    .addr(op), .data({RegDist, RegWrite, aluB, MemWrite, MemRead, busW}));  // open: sel
  ROM #(.addrWidth(5), .dataWidth(4)) rom_2 (.addr(op), .data(rom_2_data));  // open: sel
  Multiplexer #(.width(4), .enable("false")) multiplexer_1 (
    .in0({op[1:0], f}), .in1(rom_2_data), .out(aluop), .sel(comparator_1_gt));

  // Notes on the sheet:
  //   contents of rom_1 (hex, n*v repeats v):
  //   c0 c0 c0 0 60 0 60 60 4*50 4*60 69 24 4*80 62 1f0 0 142
  //   contents of rom_2 (hex, n*v repeats v):
  //   6*0 2 3 4 5 6 7 8 9 a b 0 0 1 1
endmodule

module cpu (
);

  wire _memRead, _memWrite, _RegWrite, clock_1_out, clock_2_out, clock_3_out, clock_4_out, clock_5_out,
       clock_6_out, clock_7_out, clock_8_out, clock_9_out, comparator_1_eq, comparator_2_eq, comparator_3_eq,
       comparator_4_eq, comparator_5_eq, comparator_6_eq, comparator_7_eq, comparator_8_eq, comparator_9_eq,
       comparator_10_eq, comparator_11_eq, comparator_12_eq, comparator_13_eq, comparator_14_eq, EX_MemRead,
       EX_RegWrite, Kill, Mem_RegWrite, MemRead, MemWrite, multiplexer_3_out, multiplexer_4_out,
       multiplexer_7_out, not_1_out, not_2_out, not_3_out, not_4_out, not_5_out, not_6_out, not_7_out,
       not_8_out, not_9_out, not_10_out, not_11_out, not_12_out, or_1_out, register_4_q, RegWrite, stall;
  wire [1:0] _aluB, _busW, _RegDist, aluB, busW, f, FA, FB, multiplexer_2_out, multiplexer_6_out, PcSrc,
       RegDist, register_2_q;
  wire [2:0] if_2_out, if_out, imm5, multiplexer_10_out, rd2, rd3, rd4;
  wire [3:0] _aluop, aluOp, multiplexer_8_out;
  wire [4:0] op;
  wire [5:0] imm11;
  wire [15:0] A_q, adder_1_out, adder_3_out, adder_4_out, ALUR, B_q, bit_extender_1_out, bit_extender_2_out,
       bit_extender_3_out, BusA, BusB, D_q, Data_q, imm5S, imm5Z, imm11E, MemOut, multiplexer_1_out,
       multiplexer_5_out, multiplexer_14_out, PC, PC_3_q, PC_5, PC_11, PC___1, PCX, R_q, ram_1_data,
       register_file_1_busa, register_file_1_busb, rom_1_data;

  ControlUnit controlunit_1 (
    .op(op), .f(f), .RegDist(_RegDist), .aluB(_aluB), .RegWrite(_RegWrite), .MemWrite(_memRead),
    .MemRead(_memWrite), .aluop(_aluop), .busW(_busW));
  PC pc_1 (.A(BusA), .B(BusB), .op(op), .PCsrc(PcSrc), .KILL(Kill));
  Comparator #(.width(2)) comparator_1 (.a(FA), .b(2'b01), .eq(comparator_1_eq));  // open: gt, lt
  Comparator #(.width(2)) comparator_2 (.a(FB), .b(2'b01), .eq(comparator_2_eq));  // open: gt, lt
  Adder #(.width(16)) adder_1 (.a(BusA), .b(imm5S), .out(adder_1_out));  // open: cin, cout
  or or_1 (or_1_out, comparator_1_eq, comparator_2_eq);
  Multiplexer #(.select(2), .width(16), .enable("false")) multiplexer_1 (
    .in0(PC___1), .in1(PC_5), .in2(PC_11), .in3(adder_1_out), .out(multiplexer_1_out), .sel(PcSrc));
  not not_1 (not_1_out, stall);
  Clock clock_1 (.out(clock_1_out));
  Register #(.width(16)) PC_2 (.D(multiplexer_1_out), .en(not_1_out), .Q(PC), .clk(clock_1_out));  // open: clr
  and and_1 (stall, EX_MemRead, or_1_out);
  Clock clock_2 (.out(clock_2_out));
  Register #(.width(16)) PC_3 (.D(PC), .Q(PC_3_q), .clk(clock_3_out));  // open: en, clr
  Clock clock_3 (.out(clock_3_out));
  Register #(.width(16)) PC_4 (.D(PC_3_q), .Q(PCX), .clk(clock_3_out));  // open: en, clr
  Adder #(.width(16)) adder_2 (.a(PC), .b(16'h1), .out(PC___1));  // open: cin, cout
  ROM #(.addrWidth(16), .dataWidth(16)) rom_1 (.addr(PC), .data(rom_1_data));  // open: sel
  Multiplexer #(.width(2), .enable("false")) multiplexer_2 (
    .in0(_busW), .in1(2'b00), .out(multiplexer_2_out), .sel(stall));
  Multiplexer #(.enable("false")) multiplexer_3 (.in0(_memRead), .in1(1'b0), .out(multiplexer_3_out), .sel(stall));
  Multiplexer #(.enable("false")) multiplexer_4 (.in0(_memWrite), .in1(1'b0), .out(multiplexer_4_out), .sel(stall));
  Multiplexer #(.width(16), .enable("false")) multiplexer_5 (
    .in0(rom_1_data), .in1({16{1'b0}}), .out(multiplexer_5_out), .sel(Kill));
  not not_2 (not_2_out, stall);
  Clock clock_4 (.out(clock_4_out));
  Register #(.width(2)) register_1 (.D(register_2_q), .Q(busW), .clk(clock_2_out));  // open: en, clr
  Register #(.width(2)) register_2 (.D(multiplexer_2_out), .Q(register_2_q), .clk(clock_2_out));  // open: en, clr
  Register #(.width(1)) register_3 (.D(multiplexer_3_out), .Q(EX_MemRead), .clk(clock_2_out));  // open: en, clr
  Register #(.width(1)) register_4 (.D(multiplexer_4_out), .Q(register_4_q), .clk(clock_2_out));  // open: en, clr
  Register #(.width(2)) register_5 (.D(multiplexer_6_out), .Q(aluB), .clk(clock_2_out));  // open: en, clr
  Multiplexer #(.width(2), .enable("false")) multiplexer_6 (
    .in0(_aluB), .in1(2'b00), .out(multiplexer_6_out), .sel(stall));
  Register #(.width(1)) register_6 (.D(multiplexer_7_out), .Q(EX_RegWrite), .clk(clock_2_out));  // open: en, clr
  Multiplexer #(.enable("false")) multiplexer_7 (.in0(_RegWrite), .in1(1'b0), .out(multiplexer_7_out), .sel(stall));
  Multiplexer #(.width(4), .enable("false")) multiplexer_8 (
    .in0(_aluop), .in1(4'b0000), .out(multiplexer_8_out), .sel(stall));
  Multiplexer #(.width(2), .enable("false")) multiplexer_9 (.in0(_RegDist), .in1(2'b00), .out(RegDist), .sel(stall));
  Register #(.width(16)) Inst (
    .D(multiplexer_5_out), .en(not_2_out), .Q({f, imm5, imm11, op}), .clk(clock_4_out));  // open: clr
  Register #(.width(1)) register_7 (.D(EX_MemRead), .Q(MemRead), .clk(clock_2_out));  // open: en, clr
  Register #(.width(1)) register_8 (.D(register_4_q), .Q(MemWrite), .clk(clock_2_out));  // open: en, clr
  Register #(.width(1)) register_9 (.D(EX_RegWrite), .Q(Mem_RegWrite), .clk(clock_2_out));  // open: en, clr
  Register #(.width(4)) register_10 (.D(multiplexer_8_out), .Q(aluOp), .clk(clock_2_out));  // open: en, clr
  Register #(.width(1)) register_11 (.D(Mem_RegWrite), .Q(RegWrite), .clk(clock_2_out));  // open: en, clr
  Multiplexer #(.select(2), .width(3), .enable("false")) multiplexer_10 (
    .in0(imm11[5:3]), .in1(imm5), .in2(3'b111), .in3(3'b001), .out(multiplexer_10_out), .sel(RegDist));
  register_file register_file_1 (
    .BusA(register_file_1_busa), .BusB(register_file_1_busb), .rw(rd4), .BusW(Data_q), .rs1(imm11[2:0]),
    .rs2(imm11[5:3]), .Regwrite(RegWrite));
  not not_3 (not_3_out, comparator_3_eq);
  Comparator #(.width(3)) comparator_3 (.a(imm11[2:0]), .b(3'b000), .eq(comparator_3_eq));  // open: gt, lt
  Comparator #(.width(3)) comparator_4 (.a(imm11[2:0]), .b(rd2), .eq(comparator_4_eq));  // open: gt, lt
  not not_4 (not_4_out, comparator_5_eq);
  Comparator #(.width(3)) comparator_5 (.a(imm11[2:0]), .b(3'b000), .eq(comparator_5_eq));  // open: gt, lt
  Comparator #(.width(3)) comparator_6 (.a(imm11[2:0]), .b(rd3), .eq(comparator_6_eq));  // open: gt, lt
  not not_5 (not_5_out, comparator_7_eq);
  Comparator #(.width(3)) comparator_7 (.a(imm11[2:0]), .b(3'b000), .eq(comparator_7_eq));  // open: gt, lt
  Comparator #(.width(3)) comparator_8 (.a(imm11[2:0]), .b(rd4), .eq(comparator_8_eq));  // open: gt, lt
  assign bit_extender_1_out = {{11{1'b0}}, {f, imm5}};  // Bit_Extender bit_extender_1
  assign bit_extender_2_out = {{11{f[1]}}, {f, imm5}};  // Bit_Extender bit_extender_2
  assign bit_extender_3_out = {{5{f[1]}}, {f, imm5, imm11}};  // Bit_Extender bit_extender_3
  Clock clock_5 (.out(clock_5_out));
  Register #(.width(16)) u_imm5Z (.D(bit_extender_1_out), .Q(imm5Z), .clk(clock_5_out));  // open: en, clr
  Register #(.width(16)) u_imm5S (.D(bit_extender_2_out), .Q(imm5S), .clk(clock_5_out));  // open: en, clr
  Adder #(.width(16)) adder_3 (.a(bit_extender_2_out), .b(PC), .out(adder_3_out));  // open: cin, cout
  Register #(.width(16)) imm5S_2 (.D(bit_extender_3_out), .Q(imm11E), .clk(clock_5_out));  // open: en, clr
  Adder #(.width(16)) adder_4 (.a(bit_extender_3_out), .b(PC), .out(adder_4_out));  // open: cin, cout
  Multiplexer #(.select(2), .width(16), .enable("false")) multiplexer_11 (
    .in0(register_file_1_busa), .in1(ALUR), .in2(MemOut), .in3(Data_q), .out(BusA), .sel(FA));
  Multiplexer #(.select(2), .width(16), .enable("false")) multiplexer_12 (
    .in0(register_file_1_busb), .in1(ALUR), .in2(MemOut), .in3(Data_q), .out(BusB), .sel(FB));
  and \if  (if_out[0], not_3_out, comparator_4_eq, EX_RegWrite);
  not not_6 (not_6_out, if_out[0]);
  and else_if (if_out[1], not_4_out, not_6_out, comparator_6_eq, Mem_RegWrite);
  not not_7 (not_7_out, if_out[1]);
  and else_if_2 (if_out[2], not_5_out, not_7_out, not_6_out, comparator_8_eq, RegWrite);
  Subtractor #(.width(16)) subtractor_1 (.a(adder_3_out), .b(16'h1), .out(PC_5));  // open: bin, bout
  Subtractor #(.width(16)) subtractor_2 (.a(adder_4_out), .b(16'h1), .out(PC_11));  // open: bin, bout
  Register #(.width(16)) A (.D(BusA), .Q(A_q), .clk(clock_6_out));  // open: en, clr
  Register #(.width(16)) B (.D(BusB), .Q(B_q), .clk(clock_6_out));  // open: en, clr
  Register #(.width(3)) u_RD2 (.D(multiplexer_10_out), .Q(rd2), .clk(clock_6_out));  // open: en, clr
  Clock clock_6 (.out(clock_6_out));
  Multiplexer #(.select(3), .width(2), .disabled(0), .enable("false")) multiplexer_13 (
    .in0(2'b00), .in1(2'b01), .in2(2'b10), .in3(2'b00), .in4(2'b11), .in5(2'b00), .in6(2'b00), .in7(2'b00),
    .out(FA), .sel(if_out));
  Multiplexer #(.select(2), .width(16), .enable("false")) multiplexer_14 (
    .in0(B_q), .in1(imm5Z), .in2(imm5S), .in3(imm11E), .out(multiplexer_14_out), .sel(aluB));
  ALU alu_1 (.BusA(A_q), .BusB(multiplexer_14_out), .out(ALUR), .rd(aluOp));
  Comparator #(.width(3)) comparator_9 (.a(imm11[5:3]), .b(3'b000), .eq(comparator_9_eq));  // open: gt, lt
  Comparator #(.width(3)) comparator_10 (.a(imm11[5:3]), .b(rd2), .eq(comparator_10_eq));  // open: gt, lt
  Comparator #(.width(3)) comparator_11 (.a(imm11[5:3]), .b(3'b000), .eq(comparator_11_eq));  // open: gt, lt
  Comparator #(.width(3)) comparator_12 (.a(imm11[5:3]), .b(rd3), .eq(comparator_12_eq));  // open: gt, lt
  Comparator #(.width(3)) comparator_13 (.a(imm11[5:3]), .b(3'b000), .eq(comparator_13_eq));  // open: gt, lt
  Comparator #(.width(3)) comparator_14 (.a(imm11[5:3]), .b(rd4), .eq(comparator_14_eq));  // open: gt, lt
  Register #(.width(16)) R (.D(ALUR), .Q(R_q), .clk(clock_7_out));  // open: en, clr
  Register #(.width(16)) D (.D(B_q), .Q(D_q), .clk(clock_7_out));  // open: en, clr
  Register #(.width(3)) u_RD3 (.D(rd2), .Q(rd3), .clk(clock_7_out));  // open: en, clr
  Clock clock_7 (.out(clock_7_out));
  not not_8 (not_8_out, comparator_9_eq);
  not not_9 (not_9_out, comparator_11_eq);
  not not_10 (not_10_out, comparator_13_eq);
  and if_2 (if_2_out[0], not_8_out, comparator_10_eq, EX_RegWrite);
  not not_11 (not_11_out, if_2_out[0]);
  and else_if_3 (if_2_out[1], not_9_out, not_11_out, comparator_12_eq, Mem_RegWrite);
  not not_12 (not_12_out, if_2_out[1]);
  and else_if_4 (if_2_out[2], not_10_out, not_12_out, not_11_out, comparator_14_eq, RegWrite);
  Clock clock_8 (.out(clock_8_out));
  RAM #(.addrWidth(16), .dataWidth(16), .bus("separate")) ram_1 (
    .addr(R_q), .din(D_q), .data(ram_1_data), .str(MemWrite), .clk(clock_8_out), .ld(MemRead));  // open: sel, clr
  Multiplexer #(.select(2), .width(16), .enable("false")) multiplexer_15 (
    .in0(R_q), .in1(ram_1_data), .in2(PCX), .in3(16'h1), .out(MemOut), .sel(busW));
  Register #(.width(16)) Data (.D(MemOut), .Q(Data_q), .clk(clock_9_out));  // open: en, clr
  Register #(.width(3)) u_RD4 (.D(rd3), .Q(rd4), .clk(clock_9_out));  // open: en, clr
  Clock clock_9 (.out(clock_9_out));
  Multiplexer #(.select(3), .width(2), .disabled(0), .enable("false")) multiplexer_16 (
    .in0(2'b00), .in1(2'b01), .in2(2'b10), .in3(2'b00), .in4(2'b11), .in5(2'b00), .in6(2'b00), .in7(2'b00),
    .out(FB), .sel(if_2_out));

  // Other names for the same wires on the sheet: rs[2:0] = imm11[2:0]; rt[2:0] = imm11[5:3]; imm11[10:6] = {f, imm5};
  //   rd[2:0] = imm5; imm5[4:3] = f; RW[2:0] = rd4

  // Notes on the sheet:
  //   contents of rom_1 (hex, n*v repeats v):
  //   79 2404 98 1a04 f6 1504
endmodule

module PC (
  input  [15:0] A,
  input  [15:0] B,
  input  [4:0] op,
  output [1:0] PCsrc,
  output KILL
);

  wire and_1_out, and_2_out, and_3_out, and_4_out, branchFlag, decoder_1_out18, decoder_1_out19,
       decoder_1_out20, decoder_1_out21, decoder_1_out22, decoder_1_out24, decoder_1_out25, not_1_out,
       not_2_out, Zeroflag;
  wire [2:0] Branch_out;

  Comparator #(.width(16)) comparator_1 (.a(A), .b(B), .eq(Zeroflag), .lt(branchFlag));  // open: gt
  Decoder #(.select(5), .enable("false")) decoder_1 (
    .out18(decoder_1_out18), .out19(decoder_1_out19), .out20(decoder_1_out20), .out21(decoder_1_out21),
    .out22(decoder_1_out22), .out24(decoder_1_out24), .out25(decoder_1_out25), .sel(op));  // open: out0, out1, out2, out3, out4, out5, out6, out7, out8, out9, out10, out11, out12, out13, out14, out15, out16, out17, out23, out26, out27, out28, out29, out30, out31
  not not_1 (not_1_out, Zeroflag);
  not not_2 (not_2_out, branchFlag);
  and and_1 (and_1_out, Zeroflag, decoder_1_out18);
  and and_2 (and_2_out, not_1_out, decoder_1_out19);
  and and_3 (and_3_out, decoder_1_out20, branchFlag);
  and and_4 (and_4_out, not_2_out, decoder_1_out21);
  or Branch (Branch_out[0], and_1_out, and_2_out, and_3_out, and_4_out);
  xor JAL (Branch_out[1], decoder_1_out22, 1'b0);
  or Jump (Branch_out[2], decoder_1_out24, decoder_1_out25);
  Multiplexer #(.select(3), .width(2), .enable("false")) multiplexer_1 (
    .in0(2'b00), .in1(2'b01), .in2(2'b11), .in4(2'b10), .out(PCsrc), .sel(Branch_out));  // open: in3, in5, in6, in7
  Comparator #(.width(2), .mode("unsigned")) comparator_2 (.a(PCsrc), .b(2'b00), .gt(KILL));  // open: eq, lt
endmodule
